# Fritzing sketch FritzingSchema (saved by Fritzing 0.9.4)
breadboards: 1

parts:
  Adafruit_HUZZAH_ESP8266_Breakout1 = Adafruit HUZZAH ESP8266 Breakout [part_number=2471]
  LED1 = smd LED [color="Green (555nm)" package="1206 [SMD]"]
  LED2 = smd LED [color="Blue (470nm)" package="1206 [SMD]"]
  LED3 = smd LED [color="Yellow (585nm)" package="1206 [SMD]"]
  LED4 = smd LED [color="Red (633nm)" package="1206 [SMD]"]
  R1 = Resistor [tolerance=±5% resistance=220 package="0402 [SMD]"]
  R2 = Resistor [tolerance=±5% resistance=220 package="0402 [SMD]"]
  R3 = Resistor [tolerance=±5% resistance=220 package="0402 [SMD]"]
  R4 = Resistor [tolerance=±5% resistance=220 package="0402 [SMD]"]

nets:
  N1: Adafruit_HUZZAH_ESP8266_Breakout1.GND, LED2.cathode, LED4.cathode
  N2: Adafruit_HUZZAH_ESP8266_Breakout1.#5, R4.Pin_1
  N3: Adafruit_HUZZAH_ESP8266_Breakout1.#4, R3.Pin_1
  N4: Adafruit_HUZZAH_ESP8266_Breakout1.#0, R2.Pin_1
  N5: Adafruit_HUZZAH_ESP8266_Breakout1.#2, R1.Pin_1
  N6: LED1.anode, R1.Pin_0
  N7: LED2.anode, R2.Pin_0
  N8: LED3.anode, R3.Pin_0
  N9: LED4.anode, R4.Pin_0
